# Fritzing sketch Platine_01 (saved by Fritzing 0.9.4)
perfboards: 1

parts:
  VCC1 = Battery block 9V
  JP1 = Header 5x2 [package=2x5-ra]
  JP2 = USB_MICROB_PLUG [package=micro-b-ra-th]
  JP3 = Header 5x2 [package=2x5-ra]
  M1 = RioRand LM2596
  U1 = ESP8266 WiFi Module [part_number=ESP8266]
  Bauteil1 = I2C level shifter bidirectional
  R1 = Resistor [tolerance=±5% resistance=150k package="0805 [SMD]"]
  J5 = male pin header, 1 pin [form="♂ (male)"]
  J6 = male pin header, 2 pins [form="♂ (male)"]
  J2 = male pin header, 3 pins [form="♂ (male)"]
  J3 = male pin header, 3 pins [form="♂ (male)"]
  R2 = Resistor [tolerance=±5% resistance=68 package="0805 [SMD]"]
  J7 = male pin header, 2 pins [form="♂ (male)"]
  J8 = male pin header, 2 pins [form="♂ (male)"]
  C1 = Ceramic Capacitor [capacitance=100nF package="100 mil [THT, multilayer]"]
  R3 = Resistor [tolerance=±5% resistance=4.7k package=THT]
  R4 = Resistor [tolerance=±5% resistance=4.7k package=THT]
  Q1 = Basic FET N-Channel [package="DPak [SMD]"]
  R5 = Resistor [tolerance=±5% resistance=10k package=THT]
  R6 = Resistor [tolerance=±5% resistance=1k package=THT]
  J10 = male pin header, 1 pin [form="♂ (male)"]
  J9 = male pin header, 1 pin [form="♂ (male)"]
  D1 = Rectifier Diode [part_number=1N4001 package="300 mil [THT]"]
  J11 = male pin header, 1 pin [form="♂ (male)"]
  R7 = Resistor [tolerance=±5% resistance=4.7k package=THT]

nets:
  N1: VCC1.-, JP1.2, JP1.4, JP1.6, JP1.8, JP1.10, R2.Pin_1
  N2: VCC1.+, JP1.1, JP1.3, JP1.5, JP1.7, JP1.9, R1.Pin_0, D1.cathode, J11.pin1
  N3: JP2.VCC, JP3.1, JP3.3, JP3.5, JP3.7, JP3.9, M1.Pin_1, Bauteil1.HV
  GND: JP2.GND, JP3.2, JP3.4, JP3.6, JP3.8, JP3.10, M1.Pin_2, M1.Pin_4, U1.GND, Bauteil1.GND, J3.pin1, J3.pin2, J3.pin3, C1.1
  N4: M1.Pin_3, J2.pin1, J2.pin2, J2.pin3, C1.0
  N5: U1.VCC, Bauteil1.LV, R3.Pin_0, R4.Pin_0, R7.Pin_0
  N6: U1.GPIO_0, Bauteil1.LV2, R3.Pin_1
  N7: U1.GPIO_2, Bauteil1.LV1, R4.Pin_1
  N8: U1.CH_PD, Bauteil1.LV3, J8.pin1, R7.Pin_1
  N9: Bauteil1.LV4, J8.pin2
  N10: Bauteil1.HV1, J6.pin1
  N11: Bauteil1.HV2, J6.pin2
  N12: Bauteil1.HV3, J7.pin1
  N13: Bauteil1.HV4, J7.pin2
  N14: R1.Pin_1, J5.pin1, R2.Pin_0
  N15: Q1.Gate, R5.Pin_0, R6.Pin_0
  N16: Q1.source, R5.Pin_1
  N17: R6.Pin_1, J10.pin1
  N18: J9.pin1, D1.anode

notes:
  12V Blei Akku
  _____________
  3.3 V
  5V

custom parts:
  ESP8266 WiFi Module: Generic WiFi Module based on the ESP8266 with onboard PCB antenna and UART communications
