# Fritzing sketch Platine_02v1 (saved by Fritzing 0.9.4)
circuit board: 10cm x 10cm
breadboards: 1

parts:
  IC1 = IC, DIP package, 14 pins [chip_label=IC]
  IC2 = IC, DIP package, 14 pins [chip_label=IC]
  IC3 = IC, DIP package, 14 pins [chip_label=IC]
  IC4 = IC, DIP package, 14 pins [chip_label=IC]
  IN5V = female pin header, 2 pins [form="♀ (female)"]
  JST_Connector_0 = female pin header, 10 pins [form="♀ (female)"]
  R1 = Resistor [tolerance=±5% resistance=1.5 package=THT]
  R2 = Resistor [tolerance=±5% resistance=1.5 package=THT]
  R3 = Resistor [tolerance=±5% resistance=1.5 package=THT]
  R4 = Resistor [tolerance=±5% resistance=1.5 package=THT]
  R5 = Resistor [tolerance=±5% resistance=1.5 package=THT]
  R6 = Resistor [tolerance=±5% resistance=1.5 package=THT]
  D1 = Diode [package=diode-1n4148]
  C2 = Electrolytic Capacitor [capacitance=10µF package="100 mil [THT, electrolytic]"]
  L1 = Solenoid
  D2 = Diode [package=diode-1n4148]
  C3 = Electrolytic Capacitor [capacitance=10µF package="100 mil [THT, electrolytic]"]
  L2 = Solenoid
  D3 = Diode [package=diode-1n4148]
  C4 = Electrolytic Capacitor [capacitance=10µF package="100 mil [THT, electrolytic]"]
  L3 = Solenoid
  D4 = Diode [package=diode-1n4148]
  C5 = Electrolytic Capacitor [capacitance=10µF package="100 mil [THT, electrolytic]"]
  L4 = Solenoid
  D5 = Diode [package=diode-1n4148]
  C6 = Electrolytic Capacitor [capacitance=10µF package="100 mil [THT, electrolytic]"]
  L5 = Solenoid
  D6 = Diode [package=diode-1n4148]
  C7 = Electrolytic Capacitor [capacitance=10µF package="100 mil [THT, electrolytic]"]
  L6 = Solenoid
  IN12V = female pin header, 2 pins [form="♀ (female)"]
  Q6 = NPN-Transistor [package="TO92 [THT]"]
  Q5 = NPN-Transistor [package="TO92 [THT]"]
  Q4 = NPN-Transistor [package="TO92 [THT]"]
  Q3 = NPN-Transistor [package="TO92 [THT]"]
  Q2 = NPN-Transistor [package="TO92 [THT]"]
  Q1 = NPN-Transistor [package="TO92 [THT]"]
  U1 = 74HC595 [package="DIP16 [THT]"]
  IRF4905-5 = Basic FET P-Channel [part_number=IRF4905 package="TO220 [THT]"]
  IRF4905-12 = Basic FET P-Channel [part_number=IRF4905 package="TO220 [THT]"]
  D2z = Zener Diode [part_number=1N4732A breakdown_voltage=3.6V package="300 mil [THT]"]
  D1z = Zener Diode [part_number=1N4732A breakdown_voltage=3.6V package="300 mil [THT]"]
  R7 = Resistor [tolerance=±5% resistance=1k package=THT]
  R8 = Resistor [tolerance=±5% resistance=1k package=THT]
  5V = female pin header, 2 pins [form="♀ (female)"]
  12V = female pin header, 2 pins [form="♀ (female)"]

nets:
  N1: IC1.pin1, IC1.pin4, IC1.pin10, IC1.pin13, IC2.pin1, IC2.pin4, IC2.pin10, IC2.pin13, JST_Connector_0.pin1
  N2: IC1.pin2, JST_Connector_0.pin4
  N3: IC1.pin3, IC4.pin9, IC4.pin10
  N4: IC1.pin5, JST_Connector_0.pin5
  N5: IC1.pin6, IC4.pin12, IC4.pin13
  N6: IC1.pin7, IC2.pin7, IC3.pin7, IC4.pin7, U1.GND, IRF4905-5.source, D2z.cathode, 5V.pin1
  N7: IC1.pin8, IC1.pin9, IC3.pin9, IC3.pin10, JST_Connector_0.pin9
  N8: IC1.pin11, IC1.pin12, IC3.pin12, IC3.pin13, JST_Connector_0.pin8
  N9: IC1.pin14, IC2.pin14, IC3.pin14, IC4.pin14, IN5V.pin1, U1.VCC, IRF4905-5.drain
  N10: IC2.pin2, JST_Connector_0.pin2
  N11: IC2.pin3, IC3.pin4, IC3.pin5
  N12: IC2.pin5, JST_Connector_0.pin3
  N13: IC2.pin6, IC3.pin1, IC3.pin2
  N14: IC2.pin8, IC4.pin1, IC4.pin2
  N15: IC2.pin9, JST_Connector_0.pin7
  N16: IC2.pin11, IC4.pin4, IC4.pin5
  N17: IC2.pin12, JST_Connector_0.pin6
  N18: IC3.pin3, R2.Pin_0
  N19: IC3.pin6, R1.Pin_0
  N20: IC3.pin8, R6.Pin_0
  N21: IC3.pin11, R5.Pin_0
  N22: IC4.pin8, R3.Pin_0
  N23: IC4.pin11, R4.Pin_0
  N24: IN5V.pin2, C2.-, C3.-, C4.-, C5.-, C6.-, C7.-, IN12V.pin2, Q6.E, Q5.E, Q4.E, Q3.E, Q2.E, Q1.E, R7.Pin_0, R8.Pin_0, 5V.pin2, 12V.pin2
  N25: R1.Pin_1, Q1.B
  N26: R2.Pin_1, Q2.B
  N27: R3.Pin_1, Q3.B
  N28: R4.Pin_1, Q4.B
  N29: R5.Pin_1, Q5.B
  N30: R6.Pin_1, Q6.B
  N31: D1.A, C2.+, L1.pin2, Q1.C
  N32: D1.C, L1.pin1, D2.C, L2.pin1, D3.C, L3.pin1, D4.C, L4.pin1, D5.C, L5.pin1, D6.C, L6.pin1, IRF4905-12.source, D1z.cathode, 12V.pin1
  N33: D2.A, C3.+, L2.pin2, Q2.C
  N34: D3.A, C4.+, L3.pin2, Q3.C
  N35: D4.A, C5.+, L4.pin2, Q4.C
  N36: D5.A, C6.+, L5.pin2, Q5.C
  N37: D6.A, C7.+, L6.pin2, Q6.C
  N38: IN12V.pin1, IRF4905-12.drain
  N39: IRF4905-5.gate, D2z.anode, R7.Pin_1
  N40: IRF4905-12.gate, D1z.anode, R8.Pin_1

notes:
  PWM
  Sig 0-7
  Uebertrag
  Info zener choose according to link: https://components101.com/articles/design-guide-pmos-mosfet-for-reverse-voltage-polarity-protection
