# Fritzing sketch bew_entwurf_v2_7 (saved by Fritzing 0.9.4)
circuit board: 10cm x 10cm
breadboards: 2

parts:
  R1 = Resistor [tolerance=±5% resistance=100k package=THT]
  R2 = Resistor [tolerance=±5% resistance=2k package=THT]
  R3 = Resistor [tolerance=±5% resistance=20 package=THT]
  NE555 = 555 Timer [package="DIP8 [THT]"]
  C1 = Electrolytic Capacitor [capacitance=4.7µF package="100 mil [THT, electrolytic]"]
  C3 = Ceramic Capacitor [capacitance=100nF package="100 mil [THT, multilayer]"]
  Q1 = MOSFET-NCHANNEL [package=to220v]
  R4 = Resistor [tolerance=±5% resistance=1k package=THT]
  R5 = Resistor [tolerance=±5% resistance=10k package=THT]
  S-Main = Toggle Switch [package=THT]
  Arduino_Nano = Arduino Nano (Rev3.0)
  Q2 = NPN-Transistor [package="TO92 [THT]"]
  R6 = Resistor [tolerance=±5% resistance=2k package=THT]
  C5 = Electrolytic Capacitor [capacitance=1µF package="100 mil [THT, electrolytic]"]
  C6 = Ceramic Capacitor [capacitance=100nF package="100 mil [THT, multilayer]"]
  MUX = Analog Digital MUX Breakout
  Lvl_Shft = I2C level shifter bidirectional
  R24 = Resistor [tolerance=±5% resistance=10k package=THT]
  74HC595 = 74HC595 [package="DIP16 [THT]"]
  R25 = Resistor [tolerance=±5% resistance=10k package=THT]
  Q4 = NPN-Transistor [package="TO92 [THT]"]
  R26 = Resistor [tolerance=±5% resistance=5k package=THT]
  C-MUX = Ceramic Capacitor [capacitance=100nF package="100 mil [THT, multilayer]"]
  C-BMP = Ceramic Capacitor [capacitance=100nF package="100 mil [THT, multilayer]"]
  R27 = Resistor [tolerance=±5% resistance=10k package=THT]
  R28 = Resistor [tolerance=±5% resistance=10k package=THT]
  C12 = Ceramic Capacitor [capacitance=100nF package="100 mil [THT, multilayer]"]
  C13 = Ceramic Capacitor [capacitance=100nF package="100 mil [THT, multilayer]"]
  R29 = Resistor [tolerance=±5% resistance=10k package=THT]
  R30 = Photocell (LDR) [package=THT]
  R31 = Resistor [tolerance=±5% resistance=7k package=THT]
  C-RTC = Ceramic Capacitor [capacitance=100nF package="100 mil [THT, multilayer]"]
  R32 = Resistor [tolerance=±5% resistance=10k package=THT]
  R33 = Resistor [tolerance=±5% resistance=10k package=THT]
  R34 = Resistor [tolerance=±5% resistance=10k package=THT]
  R35 = Resistor [tolerance=±5% resistance=10k package=THT]
  R36 = Resistor [tolerance=±5% resistance=10k package=THT]
  R37 = Resistor [tolerance=±5% resistance=10k package=THT]
  R38 = Resistor [tolerance=±5% resistance=10k package=THT]
  R39 = Resistor [tolerance=±5% resistance=10k package=THT]
  S2 = Toggle Switch [package=THT]
  V-Supply = Header 2 [package=screwterminal-3.5mm-2_lock]
  5V = Header 5x2 [package=2x5-ra]
  C-N = Ceramic Capacitor [capacitance=100nF package="100 mil [THT, multilayer]"]
  74HCOUT = female pin header, 9 pins [form="♀ (female)"]
  MUXOUT = rounded female pin header, 16 pins [form="♀ (female rounded)"]
  IO1 = rounded female pin header, 15 pins [form="♀ (female rounded)"]
  IO2 = rounded female pin header, 15 pins [form="♀ (female rounded)"]
  RTC-DS3231 = female pin header, 6 pins [form="♀ (female)"]
  microSD = female pin header, 6 pins [form="♀ (female)"]
  BMP/BME = female pin header, 4 pins [form="♀ (female)"]
  J5 = female pin header, 2 pins [form="♀ (female)"]
  J6 = female pin header, 2 pins [form="♀ (female)"]
  J7 = female pin header, 2 pins [form="♀ (female)"]
  T2_-_-_-_- = female pin header, 6 pins [form="♀ (female)"]
  T1_-_-_-_-_- = female pin header, 6 pins [form="♀ (female)"]

nets:
  N1: R1.Pin_0, R3.Pin_1, NE555.Reset, NE555.Vcc_Supply_Voltage, C13.1, S2.COM
  N2: R1.Pin_1, R2.Pin_0, NE555.Discharge
  N3: R2.Pin_1, NE555.Trigger, NE555.Threshold, C1.+
  N4: R3.Pin_0, NE555.Output
  GND: NE555.Ground, C1.-, C3.0, Q1.S, R5.Pin_1, S-Main.L1, Arduino_Nano.GND, Q2.E, C5.-, C6.0, MUX.GND, Lvl_Shft.GND, Q4.E, C-MUX.0, C-BMP.1, C12.0, C13.0, C-RTC.1, S2.L1, V-Supply.1, 5V.1, 5V.3, 5V.5, 5V.7, 5V.9, C-N.0, IO1.pin14, IO2.pin12, RTC-DS3231.pin6, microSD.pin1, BMP/BME.pin2
  N5: NE555.Control_Voltage, C3.1
  N6: Q1.G, R4.Pin_0, R5.Pin_0
  N7: Q1.D, T1_-_-_-_-_-.pin1, T1_-_-_-_-_-.pin2, T1_-_-_-_-_-.pin3, T1_-_-_-_-_-.pin4, T1_-_-_-_-_-.pin5, T1_-_-_-_-_-.pin6
  N8: R4.Pin_1, Arduino_Nano.D4, IO2.pin9
  VCC: S-Main.COM, Arduino_Nano.5V, C5.+, C6.1, MUX.VCC, Lvl_Shft.HV, R24.Pin_1, 74HC595.VCC, C-MUX.1, C12.1, R29.Pin_1, R30.pin_1, S2.L2, 5V.2, 5V.4, 5V.6, 5V.8, 5V.10, C-N.1, IO1.pin12, microSD.pin2
  N9: S-Main.L2, V-Supply.2
  N10: Arduino_Nano.D1/TX, IO2.pin15
  N11: Arduino_Nano.D0/RX, IO2.pin14
  N12: Arduino_Nano.RESET, IO1.pin13, IO2.pin13
  N13: Arduino_Nano.D2, IO2.pin11
  N14: Arduino_Nano.D3, R6.Pin_1, IO2.pin10
  N15: Arduino_Nano.D5, 74HC595.DS, R33.Pin_1, R38.Pin_1, IO2.pin8
  N16: Arduino_Nano.D6, 74HC595.ST_CP, R32.Pin_1, R37.Pin_1, IO2.pin7
  N17: Arduino_Nano.D7, 74HC595.SH_CP, R34.Pin_1, R36.Pin_1, IO2.pin6
  N18: Arduino_Nano.D8, R35.Pin_1, IO2.pin5
  N19: Arduino_Nano.D9, IO2.pin4
  N20: Arduino_Nano.D10, R29.Pin_0, IO2.pin3, microSD.pin6
  N21: Arduino_Nano.D11/MOSI, IO2.pin2, microSD.pin4
  N22: Arduino_Nano.D12/MISO, IO2.pin1, microSD.pin3
  N23: Arduino_Nano.VIN, IO1.pin15
  N24: Arduino_Nano.A7, IO1.pin11
  N25: Arduino_Nano.A6, IO1.pin10
  N26: Arduino_Nano.A5, Lvl_Shft.HV2, IO1.pin9
  N27: Arduino_Nano.A4, Lvl_Shft.HV1, IO1.pin8
  N28: Arduino_Nano.A3, R39.Pin_1, IO1.pin7
  N29: Arduino_Nano.A2, R26.Pin_0, IO1.pin6
  N30: Arduino_Nano.A1, MUX.SIG, IO1.pin5
  N31: Arduino_Nano.A0, IO1.pin4
  N32: Arduino_Nano.AREF, IO1.pin3
  N33: Arduino_Nano.3V3, Lvl_Shft.LV, C-BMP.0, R27.Pin_1, R28.Pin_1, C-RTC.0, IO1.pin2, RTC-DS3231.pin5, BMP/BME.pin1
  N34: Arduino_Nano.D13/SCK, IO1.pin1, microSD.pin5
  N35: Q2.B, R6.Pin_0
  N36: Q2.C, R31.Pin_0, T2_-_-_-_-.pin2, T2_-_-_-_-.pin3, T2_-_-_-_-.pin4, T2_-_-_-_-.pin5, T2_-_-_-_-.pin6
  N37: MUX.C0, MUXOUT.pin16
  N38: MUX.C1, MUXOUT.pin15
  N39: MUX.C2, MUXOUT.pin14
  N40: MUX.C3, MUXOUT.pin13
  N41: MUX.C4, MUXOUT.pin12
  N42: MUX.C5, MUXOUT.pin11
  N43: MUX.C6, MUXOUT.pin10
  N44: MUX.C7, MUXOUT.pin9
  N45: MUX.C8, MUXOUT.pin8
  N46: MUX.C9, MUXOUT.pin7
  N47: MUX.C10, MUXOUT.pin6
  N48: MUX.C11, MUXOUT.pin5
  N49: MUX.C12, MUXOUT.pin4
  N50: MUX.C13, MUXOUT.pin3
  N51: MUX.C14, MUXOUT.pin2
  N52: MUX.C15, MUXOUT.pin1
  N53: MUX.EN, R39.Pin_0
  N54: MUX.S0, R38.Pin_0
  N55: MUX.S1, R37.Pin_0
  N56: MUX.S2, R36.Pin_0
  N57: MUX.S3, R35.Pin_0
  N58: Lvl_Shft.LV4, J5.pin2
  N59: Lvl_Shft.LV3, J5.pin1
  N60: Lvl_Shft.LV2, R27.Pin_0, RTC-DS3231.pin3, BMP/BME.pin3
  N61: Lvl_Shft.LV1, R28.Pin_0, RTC-DS3231.pin4, BMP/BME.pin4
  N62: Lvl_Shft.HV3, J6.pin2
  N63: Lvl_Shft.HV4, J6.pin1
  N64: R24.Pin_0, 74HC595.MR
  N65: 74HC595.Q1, 74HCOUT.pin7
  N66: 74HC595.Q2, 74HCOUT.pin6
  N67: 74HC595.Q3, 74HCOUT.pin5
  N68: 74HC595.Q4, 74HCOUT.pin4
  N69: 74HC595.Q5, 74HCOUT.pin3
  N70: 74HC595.Q6, 74HCOUT.pin2
  N71: 74HC595.Q7, 74HCOUT.pin1
  N72: 74HC595.GND, R25.Pin_1, Q4.C, R32.Pin_0, R33.Pin_0, R34.Pin_0
  N73: 74HC595.Q7', 74HCOUT.pin9
  N74: 74HC595.OE, R25.Pin_0
  N75: 74HC595.Q0, 74HCOUT.pin8
  N76: Q4.B, R26.Pin_1
  N77: R30.pin_0, R31.Pin_1, T2_-_-_-_-.pin1
  N78: RTC-DS3231.pin1, J7.pin1
  N79: RTC-DS3231.pin2, J7.pin2

notes:
  SCL
  SDA
  VCC
  GND
  SCK
  CS
  MOSI
  MISO
  32K
  SQW
  R-p
  5V
  bewae v3 2.7
  Raaatatat
