# Fritzing sketch bewae3_3_board1v1 (saved by Fritzing 0.9.4)
circuit board: 10cm x 10cm
breadboards: 2

parts:
  C-IN-2 = Electrolytic Capacitor [capacitance=1µF package="100 mil [THT, electrolytic]"]
  C-IN-1 = Ceramic Capacitor [capacitance=100nF package="100 mil [THT, multilayer]"]
  MUX = Analog Digital MUX Breakout
  Lvl_Shft = I2C level shifter bidirectional
  R24 = Resistor [tolerance=±5% resistance=10k package=THT]
  74HC595 = 74HC595 [package="DIP16 [THT]"]
  R25 = Resistor [tolerance=±5% resistance=10k package=THT]
  C-MUX = Ceramic Capacitor [capacitance=100nF package="100 mil [THT, multilayer]"]
  R27 = Resistor [tolerance=±5% resistance=10k package=THT]
  R28 = Resistor [tolerance=±5% resistance=10k package=THT]
  C-shft = Ceramic Capacitor [capacitance=100nF package="100 mil [THT, multilayer]"]
  LDR = Photocell (LDR) [package=THT]
  rLDR = Resistor [tolerance=±5% resistance=7k package=THT]
  R32 = Resistor [tolerance=±5% resistance=10k package=THT]
  R33 = Resistor [tolerance=±5% resistance=10k package=THT]
  R34 = Resistor [tolerance=±5% resistance=10k package=THT]
  R35 = Resistor [tolerance=±5% resistance=10k package=THT]
  R36 = Resistor [tolerance=±5% resistance=10k package=THT]
  R37 = Resistor [tolerance=±5% resistance=10k package=THT]
  R38 = Resistor [tolerance=±5% resistance=10k package=THT]
  R39 = Resistor [tolerance=±5% resistance=10k package=THT]
  C-N = Ceramic Capacitor [capacitance=100nF package="100 mil [THT, multilayer]"]
  shftOUT = female pin header, 9 pins [form="♀ (female)"]
  MUXIO = rounded female pin header, 16 pins [form="♀ (female rounded)"]
  RTC-DS3231 = female pin header, 6 pins [form="♀ (female)"]
  BMP/BME = female pin header, 4 pins [form="♀ (female)"]
  5V_IN = rounded female pin header, 2 pins [form="♀ (female rounded)"]
  IRF4905_(3_3v) = Basic FET P-Channel [package="TO220 [THT]"]
  2N2222_(3_3v) = NPN-Transistor [package="TO92 [THT]"]
  R40 = Resistor [tolerance=±5% resistance=5k package=THT]
  R41 = Resistor [tolerance=±5% resistance=10k package=THT]
  ESP32 = ESP32S-HiLetgo [part_number=ESP32S-HiLetgo]
  3_3V_LM259orMP1584EN = RioRand LM2596
  IRF4905_(sens) = Basic FET P-Channel [package="TO220 [THT]"]
  2N2222_(sens) = NPN-Transistor [package="TO92 [THT]"]
  R42 = Resistor [tolerance=±5% resistance=10k package=THT]
  R43 = Resistor [tolerance=±5% resistance=5k package=THT]
  ZS-042_RTC1 = ZS-042 RTC Module
  BME280 = BME280 Breakout
  C-RTC = Ceramic Capacitor [capacitance=100nF package="100 mil [THT, multilayer]"]
  C-SD = Ceramic Capacitor [capacitance=100nF package="100 mil [THT, multilayer]"]
  C-BME = Ceramic Capacitor [capacitance=100nF package="100 mil [THT, multilayer]"]
  R44 = Resistor [tolerance=±5% resistance=220 package=THT]
  microSD = MicroSD Card Module
  SD-Slot = female pin header, 6 pins [form="♀ (female)"]
  R45 = Resistor [tolerance=±5% resistance=220 package=THT]
  R46 = Resistor [tolerance=±5% resistance=220 package=THT]
  Lvl_Shft1 = I2C level shifter bidirectional
  J1 = double row rounded female pin header, 6 pins [form="♀ (female rounded)"]
  J2 = double row rounded female pin header, 6 pins [form="♀ (female rounded)"]
  IRF4905_(sens2) = Basic FET P-Channel [package="TO220 [THT]"]
  2N2222_(sens2) = NPN-Transistor [package="TO92 [THT]"]
  R47 = Resistor [tolerance=±5% resistance=5k package=THT]
  R48 = Resistor [tolerance=±5% resistance=10k package=THT]
  logic = female pin header, 2 pins [form="♀ (female)"]
  sens2 = female pin header, 2 pins [form="♀ (female)"]
  RL1 = Resistor [tolerance=±5% resistance=4.7k package=THT]
  RL2 = Resistor [tolerance=±5% resistance=4.7k package=THT]
  RL3 = Resistor [tolerance=±5% resistance=4.7k package=THT]

nets:
  GND: C-IN-2.-, C-IN-1.0, MUX.GND, Lvl_Shft.GND, 74HC595.GND, R25.Pin_1, C-MUX.0, C-shft.0, rLDR.Pin_0, R32.Pin_0, R33.Pin_0, R34.Pin_0, C-N.0, RTC-DS3231.pin6, BMP/BME.pin2, 5V_IN.pin2, 2N2222_(3_3v).E, ESP32.GND, 3_3V_LM259orMP1584EN.Pin_2, 3_3V_LM259orMP1584EN.Pin_4, 2N2222_(sens).E, ZS-042_RTC1.GND, BME280.GND, C-RTC.1, C-SD.0, C-BME.1, microSD.GND, SD-Slot.pin1, R46.Pin_0, Lvl_Shft1.GND, J1.pin4, J1.pin5, J1.pin6, J2.pin4, J2.pin5, J2.pin6, 2N2222_(sens2).E, logic.pin2, RL3.Pin_0
  N1: C-IN-2.+, C-IN-1.1, Lvl_Shft.HV, C-N.1, 5V_IN.pin1, IRF4905_(3_3v).source, R41.Pin_0, ESP32.VIN, IRF4905_(sens).source, R42.Pin_0, R44.Pin_0, Lvl_Shft1.HV, J1.pin1, J1.pin2, J1.pin3
  N2: MUX.C0, MUXIO.pin16
  N3: MUX.C1, MUXIO.pin15
  N4: MUX.C2, MUXIO.pin14
  N5: MUX.C3, MUXIO.pin13
  N6: MUX.C4, MUXIO.pin12
  N7: MUX.C5, MUXIO.pin11
  N8: MUX.C6, MUXIO.pin10
  N9: MUX.C7, MUXIO.pin9
  N10: MUX.C8, MUXIO.pin8
  N11: MUX.C9, MUXIO.pin7
  N12: MUX.C10, MUXIO.pin6
  N13: MUX.C11, MUXIO.pin5
  N14: MUX.C12, MUXIO.pin4
  N15: MUX.C13, MUXIO.pin3
  N16: MUX.C14, MUXIO.pin2
  N17: MUX.C15, LDR.pin_0, rLDR.Pin_1, MUXIO.pin1
  VCC: MUX.VCC, C-MUX.1, LDR.pin_1, IRF4905_(sens).drain, C-SD.1, microSD.VCC, SD-Slot.pin2, RL1.Pin_0
  N18: MUX.EN, R39.Pin_0
  N19: MUX.S0, R38.Pin_0
  N20: MUX.S1, R37.Pin_0
  N21: MUX.S2, R36.Pin_0
  N22: MUX.S3, R35.Pin_0
  N23: MUX.SIG, R45.Pin_1
  N24: Lvl_Shft.LV4, ESP32.GPIO15
  N25: Lvl_Shft.LV3, ESP32.GPIO13
  VCC_2: Lvl_Shft.LV, R24.Pin_1, 74HC595.VCC, R27.Pin_1, R28.Pin_1, C-shft.1, RTC-DS3231.pin5, BMP/BME.pin1, 3_3V_LM259orMP1584EN.Pin_3, ZS-042_RTC1.VCC, BME280.3.3V, C-RTC.0, C-BME.0, Lvl_Shft1.LV, J2.pin1, J2.pin2, J2.pin3, IRF4905_(sens2).source, R48.Pin_0, logic.pin1
  N26: Lvl_Shft.LV2, ESP32.GPIO12
  N27: Lvl_Shft.LV1, ESP32.GPIO14
  N28: Lvl_Shft.HV1, microSD.SCK, SD-Slot.pin5
  N29: Lvl_Shft.HV2, microSD.MISO, SD-Slot.pin3
  N30: Lvl_Shft.HV3, microSD.MOSI, SD-Slot.pin4
  N31: Lvl_Shft.HV4, R44.Pin_1, microSD.CS, SD-Slot.pin6
  N32: R24.Pin_0, 74HC595.MR
  N33: 74HC595.Q1, shftOUT.pin7
  N34: 74HC595.Q2, shftOUT.pin6
  N35: 74HC595.Q3, shftOUT.pin5
  N36: 74HC595.Q4, shftOUT.pin4
  N37: 74HC595.Q5, shftOUT.pin3
  N38: 74HC595.Q6, shftOUT.pin2
  N39: 74HC595.Q7, shftOUT.pin1
  N40: 74HC595.SH_CP, R34.Pin_1, ESP32.GPIO27
  N41: 74HC595.ST_CP, R32.Pin_1, ESP32.GPIO26
  N42: 74HC595.OE, R25.Pin_0
  N43: 74HC595.DS, R33.Pin_1, ESP32.GPIO33
  N44: 74HC595.Q0, shftOUT.pin8
  N45: R27.Pin_0, RTC-DS3231.pin3, BMP/BME.pin3, ESP32.GPIO22, ZS-042_RTC1.SCL, BME280.SCK/SCL
  N46: R28.Pin_0, RTC-DS3231.pin4, BMP/BME.pin4, ESP32.GPIO21, ZS-042_RTC1.SDA, BME280.SDI/SDA
  N47: R35.Pin_1, Lvl_Shft1.HV1
  N48: R36.Pin_1, Lvl_Shft1.HV2
  N49: R37.Pin_1, Lvl_Shft1.HV3
  N50: R38.Pin_1, Lvl_Shft1.HV4
  N51: R39.Pin_1, ESP32.GPIO5
  N52: shftOUT.pin9, ESP32.GPIO32
  N53: RTC-DS3231.pin1, ZS-042_RTC1.32K
  N54: RTC-DS3231.pin2, ZS-042_RTC1.SQW
  N55: IRF4905_(3_3v).gate, 2N2222_(3_3v).C, R41.Pin_1
  N56: IRF4905_(3_3v).drain, 3_3V_LM259orMP1584EN.Pin_1, RL3.Pin_1
  N57: 2N2222_(3_3v).B, R40.Pin_0
  N58: R40.Pin_1, ESP32.GPIO23
  N59: ESP32.GPIO39, R45.Pin_0, R46.Pin_1
  N60: ESP32.GPIO4, R43.Pin_1
  N61: ESP32.GPIO16, Lvl_Shft1.LV1
  N62: ESP32.GPIO17, Lvl_Shft1.LV2
  N63: ESP32.GPIO18, Lvl_Shft1.LV3
  N64: ESP32.GPIO19, Lvl_Shft1.LV4
  N65: IRF4905_(sens).gate, 2N2222_(sens).C, R42.Pin_1, RL1.Pin_1
  N66: 2N2222_(sens).B, R43.Pin_0
  N67: IRF4905_(sens2).gate, 2N2222_(sens2).C, R48.Pin_1, sens2.pin2, RL2.Pin_1
  N68: IRF4905_(sens2).drain, sens2.pin1, RL2.Pin_0
  N69: 2N2222_(sens2).B, R47.Pin_0

notes:
  SCL
  SDA
  VCC
  GND
  SCK
  CS
  MOSI
  MISO
  32K
  SQW
  5V
  br-mat (c) 2022
  Board 1
  bewae v3.3
  github.com/br-mat
  3.3V
  2
  3
  4
  5
  6
  7
  0
  1
  PWM
  + -

custom parts:
  ESP32S-HiLetgo: HiLetgo ESP-WROOM-32 ESP32 ESP-32S Development Board 2.4GHz Dual-Mode WiFi + Bluetooth Dual Cores Microcontroller The ESP32 integrated with Antenna switches, RF Balun, power amplifiers, low-noise amplifiers, filters, and management modules, and the entire solution occupies the least area of PCB. 2.4 GHz Wi-Fi plus Bluetooth dual-mode chip, with TSMC Ultra-low power consumption 40nm technology,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
