# Fritzing sketch bewae3_3_board2v1 (saved by Fritzing 0.9.4)
circuit board: 10cm x 10cm
breadboards: 1

parts:
  IC1 = IC, DIP package, 14 pins [chip_label=IC]
  IC2 = IC, DIP package, 14 pins [chip_label=IC]
  IC3 = IC, DIP package, 14 pins [chip_label=IC]
  IC4 = IC, DIP package, 14 pins [chip_label=IC]
  5V_IN = female pin header, 2 pins [form="♀ (female)"]
  R1 = Resistor [tolerance=±5% resistance=1.5 package=THT]
  R2 = Resistor [tolerance=±5% resistance=1.5 package=THT]
  R3 = Resistor [tolerance=±5% resistance=1.5 package=THT]
  R4 = Resistor [tolerance=±5% resistance=1.5 package=THT]
  R5 = Resistor [tolerance=±5% resistance=1.5 package=THT]
  R6 = Resistor [tolerance=±5% resistance=1.5 package=THT]
  D1 = Diode [package=diode-1n4148]
  C2 = Electrolytic Capacitor [capacitance=10µF package="100 mil [THT, electrolytic]"]
  L1 = Solenoid
  D2 = Diode [package=diode-1n4148]
  C3 = Electrolytic Capacitor [capacitance=10µF package="100 mil [THT, electrolytic]"]
  L2 = Solenoid
  D3 = Diode [package=diode-1n4148]
  C4 = Electrolytic Capacitor [capacitance=10µF package="100 mil [THT, electrolytic]"]
  L3 = Solenoid
  D4 = Diode [package=diode-1n4148]
  C5 = Electrolytic Capacitor [capacitance=10µF package="100 mil [THT, electrolytic]"]
  L4 = Solenoid
  D5 = Diode [package=diode-1n4148]
  C6 = Electrolytic Capacitor [capacitance=10µF package="100 mil [THT, electrolytic]"]
  L5 = Solenoid
  D6 = Diode [package=diode-1n4148]
  C7 = Electrolytic Capacitor [capacitance=10µF package="100 mil [THT, electrolytic]"]
  L6 = Solenoid
  12V_IN = female pin header, 2 pins [form="♀ (female)"]
  Q6 = NPN-Transistor [package="TO92 [THT]"]
  Q5 = NPN-Transistor [package="TO92 [THT]"]
  Q4 = NPN-Transistor [package="TO92 [THT]"]
  Q3 = NPN-Transistor [package="TO92 [THT]"]
  Q2 = NPN-Transistor [package="TO92 [THT]"]
  Q1 = NPN-Transistor [package="TO92 [THT]"]
  5V_Sw = Toggle Switch [package=THT]
  12V_Sw = Toggle Switch [package=THT]
  JST_0_(9_Pin) = rounded female pin header, 9 pins [form="♀ (female rounded)"]
  POW_B1 = rounded female pin header, 2 pins [form="♀ (female rounded)"]
  R7 = Resistor [tolerance=±5% resistance=220 package=THT]
  5V_POW = LED - 5mm [color="Red (633nm)" package="5 mm [THT]"]
  SENS0 = rounded female pin header, 3 pins [form="♀ (female rounded)"]
  SENS1 = rounded female pin header, 3 pins [form="♀ (female rounded)"]
  SENS2 = rounded female pin header, 3 pins [form="♀ (female rounded)"]
  SENS3 = rounded female pin header, 3 pins [form="♀ (female rounded)"]
  SENS4 = rounded female pin header, 3 pins [form="♀ (female rounded)"]
  SENS5 = rounded female pin header, 3 pins [form="♀ (female rounded)"]
  SENS6 = rounded female pin header, 3 pins [form="♀ (female rounded)"]
  SENS7 = rounded female pin header, 3 pins [form="♀ (female rounded)"]
  SENS8 = rounded female pin header, 3 pins [form="♀ (female rounded)"]
  SENS9 = rounded female pin header, 3 pins [form="♀ (female rounded)"]
  LOGIC = rounded female pin header, 2 pins [form="♀ (female rounded)"]
  sens2 = rounded female pin header, 2 pins [form="♀ (female rounded)"]
  SENS_4-0 = rounded female pin header, 5 pins [form="♀ (female rounded)"]
  SENS_9-5 = rounded female pin header, 5 pins [form="♀ (female rounded)"]
  Q7 = Basic FET N-Channel [package="TO220 [THT]"]
  R8 = Resistor [tolerance=±5% resistance=3.3k package=THT]
  R9 = Resistor [tolerance=±5% resistance=20k package=THT]
  C8 = Electrolytic Capacitor [capacitance=10µF package="100 mil [THT, electrolytic]"]
  D7 = Diode [package=diode-1n4148]
  L7 = Solenoid
  D8 = Diode [package=diode-1n4148]
  C9 = Electrolytic Capacitor [capacitance=10µF package="100 mil [THT, electrolytic]"]
  L8 = Solenoid
  Q8 = Basic FET N-Channel [package="TO220 [THT]"]
  R10 = Resistor [tolerance=±5% resistance=3.3k package=THT]
  R11 = Resistor [tolerance=±5% resistance=20k package=THT]

nets:
  N1: IC1.pin1, IC1.pin4, IC1.pin10, IC1.pin13, IC2.pin1, IC2.pin4, IC2.pin10, IC2.pin13, JST_0_(9_Pin).pin1
  N2: IC1.pin2, JST_0_(9_Pin).pin4
  N3: IC1.pin3, IC4.pin9, IC4.pin10
  N4: IC1.pin5, JST_0_(9_Pin).pin5
  N5: IC1.pin6, IC4.pin12, IC4.pin13
  N6: IC1.pin7, IC2.pin7, IC3.pin7, IC4.pin7, 5V_IN.pin2, C2.-, C3.-, C4.-, C5.-, C6.-, C7.-, 12V_IN.pin2, Q6.E, Q5.E, Q4.E, Q3.E, Q2.E, Q1.E, 5V_Sw.L1, 12V_Sw.L1, POW_B1.pin2, R7.Pin_1, SENS0.pin3, SENS1.pin3, SENS2.pin3, SENS3.pin3, SENS4.pin3, SENS5.pin3, SENS6.pin3, SENS7.pin3, SENS8.pin3, SENS9.pin3, LOGIC.pin2, sens2.pin2, Q7.source, R9.Pin_1, C8.-, C9.-, Q8.source, R11.Pin_1
  N7: IC1.pin8, IC3.pin9, IC3.pin10
  N8: IC1.pin9, JST_0_(9_Pin).pin9
  N9: IC1.pin11, IC3.pin12, IC3.pin13
  N10: IC1.pin12, JST_0_(9_Pin).pin8
  N11: IC1.pin14, IC2.pin14, IC3.pin14, IC4.pin14, LOGIC.pin1
  N12: IC2.pin2, JST_0_(9_Pin).pin2
  N13: IC2.pin3, IC3.pin4, IC3.pin5
  N14: IC2.pin5, JST_0_(9_Pin).pin3
  N15: IC2.pin6, IC3.pin1, IC3.pin2
  N16: IC2.pin8, IC4.pin1, IC4.pin2
  N17: IC2.pin9, JST_0_(9_Pin).pin7
  N18: IC2.pin11, IC4.pin4, IC4.pin5
  N19: IC2.pin12, JST_0_(9_Pin).pin6
  N20: IC3.pin3, R2.Pin_0
  N21: IC3.pin6, R1.Pin_0
  N22: IC3.pin8, R6.Pin_0
  N23: IC3.pin11, R5.Pin_0
  N24: IC4.pin3, R10.Pin_1
  N25: IC4.pin6, R8.Pin_1
  N26: IC4.pin8, R3.Pin_0
  N27: IC4.pin11, R4.Pin_0
  N28: 5V_IN.pin1, 5V_Sw.L2
  N29: R1.Pin_1, Q1.B
  N30: R2.Pin_1, Q2.B
  N31: R3.Pin_1, Q3.B
  N32: R4.Pin_1, Q4.B
  N33: R5.Pin_1, Q5.B
  N34: R6.Pin_1, Q6.B
  N35: D1.A, C2.+, L1.pin2, Q1.C
  N36: D1.C, L1.pin1, D2.C, L2.pin1, D3.C, L3.pin1, D4.C, L4.pin1, D5.C, L5.pin1, D6.C, L6.pin1, 12V_Sw.COM, D7.C, L7.pin2, D8.C, L8.pin2
  N37: D2.A, C3.+, L2.pin2, Q2.C
  N38: D3.A, C4.+, L3.pin2, Q3.C
  N39: D4.A, C5.+, L4.pin2, Q4.C
  N40: D5.A, C6.+, L5.pin2, Q5.C
  N41: D6.A, C7.+, L6.pin2, Q6.C
  N42: 12V_IN.pin1, 12V_Sw.L2
  N43: 5V_Sw.COM, POW_B1.pin1, 5V_POW.anode
  N44: R7.Pin_0, 5V_POW.cathode
  N45: SENS0.pin1, SENS1.pin1, SENS2.pin1, SENS3.pin1, SENS4.pin1, SENS5.pin1, SENS6.pin1, SENS7.pin1, SENS8.pin1, SENS9.pin1, sens2.pin1
  N46: SENS0.pin2, SENS_4-0.pin5
  N47: SENS1.pin2, SENS_4-0.pin4
  N48: SENS2.pin2, SENS_4-0.pin3
  N49: SENS3.pin2, SENS_4-0.pin2
  N50: SENS4.pin2, SENS_4-0.pin1
  N51: SENS5.pin2, SENS_9-5.pin5
  N52: SENS6.pin2, SENS_9-5.pin4
  N53: SENS7.pin2, SENS_9-5.pin3
  N54: SENS8.pin2, SENS_9-5.pin2
  N55: SENS9.pin2, SENS_9-5.pin1
  N56: Q7.gate, R8.Pin_0, R9.Pin_0
  N57: Q7.drain, C8.+, D7.A, L7.pin1
  N58: D8.A, C9.+, L8.pin1, Q8.drain
  N59: Q8.gate, R10.Pin_0, R11.Pin_0

notes:
  PWM
  Sig 0-7
  Uebertrag
  P3
  P2
  P1
  P0
  P6
  P5
  P4
  P7
  - +
  + -
  github.com/br-mat
  bewae v3.2
  Board 2
  br-mat
  br-mat (c) 2022
  bewae v3.3
