# Fritzing sketch bewae3_3_board3v22 (saved by Fritzing 0.9.4)
circuit board: 10cm x 10cm
breadboards: 1

parts:
  R1 = Resistor [tolerance=±5% resistance=1.5k package=THT]
  R2 = Resistor [tolerance=±5% resistance=1.5k package=THT]
  R3 = Resistor [tolerance=±5% resistance=1.5k package=THT]
  R4 = Resistor [tolerance=±5% resistance=1.5k package=THT]
  R5 = Resistor [tolerance=±5% resistance=1.5k package=THT]
  R6 = Resistor [tolerance=±5% resistance=1.5 package=THT]
  D1 = Diode [package=diode-1n4148]
  C2 = Electrolytic Capacitor [capacitance=10µF package="100 mil [THT, electrolytic]"]
  L1 = Solenoid
  D2 = Diode [package=diode-1n4148]
  C3 = Electrolytic Capacitor [capacitance=10µF package="100 mil [THT, electrolytic]"]
  L2 = Solenoid
  D3 = Diode [package=diode-1n4148]
  C4 = Electrolytic Capacitor [capacitance=10µF package="100 mil [THT, electrolytic]"]
  L3 = Solenoid
  D4 = Diode [package=diode-1n4148]
  C5 = Electrolytic Capacitor [capacitance=10µF package="100 mil [THT, electrolytic]"]
  L4 = Solenoid
  D5 = Diode [package=diode-1n4148]
  C6 = Electrolytic Capacitor [capacitance=10µF package="100 mil [THT, electrolytic]"]
  L5 = Solenoid
  D6 = Diode [package=diode-1n4148]
  C7 = Electrolytic Capacitor [capacitance=10µF package="100 mil [THT, electrolytic]"]
  L6 = Solenoid
  12V_IN = female pin header, 2 pins [form="♀ (female)"]
  Q6 = NPN-Transistor [package="TO92 [THT]"]
  Q5 = NPN-Transistor [package="TO92 [THT]"]
  Q4 = NPN-Transistor [package="TO92 [THT]"]
  Q3 = NPN-Transistor [package="TO92 [THT]"]
  Q2 = NPN-Transistor [package="TO92 [THT]"]
  Q1 = NPN-Transistor [package="TO92 [THT]"]
  5V_Sw = Toggle Switch [package=THT]
  12V_Sw = Toggle Switch [package=THT]
  JST_0_(9_Pin) = rounded female pin header, 9 pins [form="♀ (female rounded)"]
  POW_B1 = rounded female pin header, 2 pins [form="♀ (female rounded)"]
  R7 = Resistor [tolerance=±5% resistance=220 package=THT]
  5V_POW = LED - 5mm [color="Red (633nm)" package="5 mm [THT]"]
  SENS0 = rounded female pin header, 3 pins [form="♀ (female rounded)"]
  SENS1 = rounded female pin header, 3 pins [form="♀ (female rounded)"]
  SENS2 = rounded female pin header, 3 pins [form="♀ (female rounded)"]
  SENS3 = rounded female pin header, 3 pins [form="♀ (female rounded)"]
  SENS4 = rounded female pin header, 3 pins [form="♀ (female rounded)"]
  SENS5 = rounded female pin header, 3 pins [form="♀ (female rounded)"]
  SENS6 = rounded female pin header, 3 pins [form="♀ (female rounded)"]
  SENS7 = rounded female pin header, 3 pins [form="♀ (female rounded)"]
  SENS8 = rounded female pin header, 3 pins [form="♀ (female rounded)"]
  SENS9 = rounded female pin header, 3 pins [form="♀ (female rounded)"]
  LOGIC = rounded female pin header, 2 pins [form="♀ (female rounded)"]
  sens2 = rounded female pin header, 2 pins [form="♀ (female rounded)"]
  SENS_4-0 = rounded female pin header, 5 pins [form="♀ (female rounded)"]
  SENS_9-5 = rounded female pin header, 5 pins [form="♀ (female rounded)"]
  Q7 = Basic FET N-Channel [package="TO220 [THT]"]
  R9 = Resistor [tolerance=±5% resistance=20k package=THT]
  C8 = Electrolytic Capacitor [capacitance=10µF package="100 mil [THT, electrolytic]"]
  D7 = Diode [package=diode-1n4148]
  L7 = Solenoid
  D8 = Diode [package=diode-1n4148]
  C9 = Electrolytic Capacitor [capacitance=10µF package="100 mil [THT, electrolytic]"]
  L8 = Solenoid
  Q8 = Basic FET N-Channel [package="TO220 [THT]"]
  R11 = Resistor [tolerance=±5% resistance=20k package=THT]
  R12 = Resistor [tolerance=±5% resistance=68k package=THT]
  R13 = Resistor [tolerance=±5% resistance=22k package=THT]
  SENS_14-10 = rounded female pin header, 5 pins [form="♀ (female rounded)"]
  SENS10 = rounded female pin header, 3 pins [form="♀ (female rounded)"]
  SENS11 = rounded female pin header, 3 pins [form="♀ (female rounded)"]
  SENS12 = rounded female pin header, 3 pins [form="♀ (female rounded)"]
  s13 = rounded female pin header, 1 pin [form="♀ (female rounded)"]
  5V_GND = double row rounded female pin header, 4 pins [form="♀ (female rounded)"]
  IRF4905_5V = Basic FET P-Channel [package="TO220 [THT]"]
  IRF4905_12V = Basic FET P-Channel [package="TO220 [THT]"]
  1N4730 = DIODE-ZENER [package=diode-zener]
  1N4737 = DIODE-ZENER [package=diode-zener]
  R14 = Resistor [tolerance=±5% resistance=20k package=THT]
  R15 = Resistor [tolerance=±5% resistance=10k package=THT]
  C_b1 = Electrolytic Capacitor [capacitance=1µF package="100 mil [THT, electrolytic]"]
  5V_IN = female pin header, 2 pins [form="♀ (female)"]
  12V_POW = LED - 5mm [color="Red (633nm)" package="5 mm [THT]"]
  R16 = Resistor [tolerance=±5% resistance=220 package=THT]
  74HC595 = 74HC595 [package="DIP16 [THT]"]
  R17 = Resistor [tolerance=±5% resistance=10k package=THT]
  R18 = Resistor [tolerance=±5% resistance=10k package=THT]
  R19 = Resistor [tolerance=±5% resistance=10k package=THT]
  R20 = Resistor [tolerance=±5% resistance=10k package=THT]
  R21 = Resistor [tolerance=±5% resistance=10k package=THT]
  Q9 = NPN-Transistor [package="TO92 [THT]"]
  Q10 = NPN-Transistor [package="TO92 [THT]"]
  Q11 = NPN-Transistor [package="TO92 [THT]"]
  Q12 = NPN-Transistor [package="TO92 [THT]"]
  R22 = Resistor [tolerance=±5% resistance=1.5k package=THT]
  R23 = Resistor [tolerance=±5% resistance=1.5k package=THT]
  R24 = Resistor [tolerance=±5% resistance=1.5k package=THT]
  R25 = Resistor [tolerance=±5% resistance=1.5k package=THT]
  R26 = Resistor [tolerance=±5% resistance=1.5k package=THT]
  R27 = Resistor [tolerance=±5% resistance=1.5k package=THT]
  D9 = Diode [package=diode-1n4148]
  D10 = Diode [package=diode-1n4148]
  D11 = Diode [package=diode-1n4148]
  D12 = Diode [package=diode-1n4148]
  D13 = Diode [package=diode-1n4148]
  D14 = Diode [package=diode-1n4148]
  C10 = Electrolytic Capacitor [capacitance=10µF package="100 mil [THT, electrolytic]"]
  C11 = Electrolytic Capacitor [capacitance=10µF package="100 mil [THT, electrolytic]"]
  C12 = Electrolytic Capacitor [capacitance=10µF package="100 mil [THT, electrolytic]"]
  C13 = Electrolytic Capacitor [capacitance=10µF package="100 mil [THT, electrolytic]"]
  C14 = Electrolytic Capacitor [capacitance=10µF package="100 mil [THT, electrolytic]"]
  C15 = Electrolytic Capacitor [capacitance=10µF package="100 mil [THT, electrolytic]"]
  L9 = Solenoid
  L10 = Solenoid
  L11 = Solenoid
  L12 = Solenoid
  L13 = Solenoid
  L14 = Solenoid
  Q13 = NPN-Transistor [package="TO92 [THT]"]
  Q14 = NPN-Transistor [package="TO92 [THT]"]
  C-shft = Ceramic Capacitor [capacitance=100nF package="100 mil [THT, multilayer]"]
  6_7 = female pin header, 2 pins [form="♀ (female)"]
  qs--sh--st = female pin header, 3 pins [form="♀ (female)"]

nets:
  N1: R1.Pin_0, JST_0_(9_Pin).pin4
  N2: R1.Pin_1, Q1.B
  N3: R2.Pin_0, JST_0_(9_Pin).pin5
  N4: R2.Pin_1, Q2.B
  N5: R3.Pin_0, JST_0_(9_Pin).pin6
  N6: R3.Pin_1, Q3.B
  N7: R4.Pin_0, JST_0_(9_Pin).pin7
  N8: R4.Pin_1, Q4.B
  N9: R5.Pin_0, JST_0_(9_Pin).pin8
  N10: R5.Pin_1, Q5.B
  N11: R6.Pin_0, JST_0_(9_Pin).pin9
  N12: R6.Pin_1, Q6.B
  N13: D1.A, C2.+, L1.pin2, Q1.C
  N14: D1.C, L1.pin1, D2.C, L2.pin1, D3.C, L3.pin1, D4.C, L4.pin1, D5.C, L5.pin1, D6.C, L6.pin1, 12V_Sw.COM, D7.C, L7.pin2, D8.C, L8.pin2, R12.Pin_1, 12V_POW.anode, D9.C, D10.C, D11.C, D12.C, D13.C, D14.C, L9.pin1, L10.pin1, L11.pin1, L12.pin1, L13.pin1, L14.pin1
  N15: C2.-, C3.-, C4.-, C5.-, C6.-, C7.-, 12V_IN.pin2, Q6.E, Q5.E, Q4.E, Q3.E, Q2.E, Q1.E, 5V_Sw.L1, 12V_Sw.L1, POW_B1.pin2, R7.Pin_1, SENS0.pin3, SENS1.pin3, SENS2.pin3, SENS3.pin3, SENS4.pin3, SENS5.pin3, SENS6.pin3, SENS7.pin3, SENS8.pin3, SENS9.pin3, LOGIC.pin2, sens2.pin2, Q7.source, R9.Pin_1, C8.-, C9.-, Q8.source, R11.Pin_1, R13.Pin_0, SENS10.pin2, SENS11.pin2, SENS12.pin2, 5V_GND.pin2, 5V_GND.pin3, R14.Pin_0, R15.Pin_0, C_b1.-, 5V_IN.pin2, R16.Pin_1, 74HC595.GND, R18.Pin_1, R19.Pin_1, R20.Pin_1, R21.Pin_1, Q9.E, Q10.E, Q11.E, Q12.E, C10.-, C11.-, C12.-, C13.-, C14.-, C15.-, Q13.E, Q14.E, C-shft.0
  N16: D2.A, C3.+, L2.pin2, Q2.C
  N17: D3.A, C4.+, L3.pin2, Q3.C
  N18: D4.A, C5.+, L4.pin2, Q4.C
  N19: D5.A, C6.+, L5.pin2, Q5.C
  N20: D6.A, C7.+, L6.pin2, Q6.C
  N21: 12V_IN.pin1, IRF4905_12V.drain
  N22: 5V_Sw.COM, POW_B1.pin1, 5V_POW.anode, C_b1.+
  N23: 5V_Sw.L2, IRF4905_5V.source, 1N4730.C
  N24: 12V_Sw.L2, IRF4905_12V.source, 1N4737.C
  N25: JST_0_(9_Pin).pin1, 74HC595.OE, R19.Pin_0
  N26: JST_0_(9_Pin).pin2, Q8.gate, R11.Pin_0
  N27: JST_0_(9_Pin).pin3, Q7.gate, R9.Pin_0
  N28: R7.Pin_0, 5V_POW.cathode
  N29: SENS0.pin1, SENS1.pin1, SENS2.pin1, SENS3.pin1, SENS4.pin1, SENS5.pin1, SENS6.pin1, SENS7.pin1, SENS8.pin1, SENS9.pin1, sens2.pin1
  N30: SENS0.pin2, SENS_4-0.pin5
  N31: SENS1.pin2, SENS_4-0.pin4
  N32: SENS2.pin2, SENS_4-0.pin3
  N33: SENS3.pin2, SENS_4-0.pin2
  N34: SENS4.pin2, SENS_4-0.pin1
  N35: SENS5.pin2, SENS_9-5.pin5
  N36: SENS6.pin2, SENS_9-5.pin4
  N37: SENS7.pin2, SENS_9-5.pin3
  N38: SENS8.pin2, SENS_9-5.pin2
  N39: SENS9.pin2, SENS_9-5.pin1
  N40: LOGIC.pin1, 5V_GND.pin1, 5V_GND.pin4, 74HC595.VCC, R17.Pin_0, C-shft.1
  N41: Q7.drain, C8.+, D7.A, L7.pin1
  N42: D8.A, C9.+, L8.pin1, Q8.drain
  N43: R12.Pin_0, R13.Pin_1, SENS_14-10.pin1
  N44: SENS_14-10.pin2, s13.pin1
  N45: SENS_14-10.pin3, SENS11.pin3
  N46: SENS_14-10.pin4, SENS12.pin3
  N47: SENS_14-10.pin5, SENS10.pin3
  N48: SENS10.pin1, SENS11.pin1, SENS12.pin1
  N49: IRF4905_5V.gate, 1N4730.A, R15.Pin_1
  N50: IRF4905_5V.drain, 5V_IN.pin1
  N51: IRF4905_12V.gate, 1N4737.A, R14.Pin_1
  N52: 12V_POW.cathode, R16.Pin_0
  N53: 74HC595.Q1, R26.Pin_0
  N54: 74HC595.Q2, R25.Pin_0
  N55: 74HC595.Q3, R24.Pin_0
  N56: 74HC595.Q4, R23.Pin_0
  N57: 74HC595.Q5, R22.Pin_0
  N58: 74HC595.Q6, 6_7.pin1
  N59: 74HC595.Q7, 6_7.pin2
  N60: 74HC595.MR, R17.Pin_1
  N61: 74HC595.SH_CP, R21.Pin_0, qs--sh--st.pin2
  N62: 74HC595.ST_CP, R20.Pin_0, qs--sh--st.pin3
  N63: 74HC595.DS, R18.Pin_0, qs--sh--st.pin1
  N64: 74HC595.Q0, R27.Pin_0
  N65: Q9.B, R27.Pin_1
  N66: Q9.C, D14.A, C15.+, L14.pin2
  N67: Q10.B, R25.Pin_1
  N68: Q10.C, D12.A, C13.+, L12.pin2
  N69: Q11.B, R23.Pin_1
  N70: Q11.C, D10.A, C11.+, L10.pin2
  N71: Q12.B, R22.Pin_1
  N72: Q12.C, D9.A, C10.+, L9.pin2
  N73: R24.Pin_1, Q13.B
  N74: R26.Pin_1, Q14.B
  N75: D11.A, C12.+, L11.pin2, Q13.C
  N76: D13.A, C14.+, L13.pin2, Q14.C

notes:
  PWM
  Sig 0-7
  Uebertrag
  P0 P1 P2 P3 P4 P5 P6 P7
  - +
  + -
  br-mat (c) 2023
  bewae v3.3
  Board 3v2
  github.com/br-mat
  +
  -
