# Fritzing sketch bewae3_3_board5v5_final (saved by Fritzing 0.9.4)
circuit board: 10cm x 10cm
breadboards: 2

parts:
  C-IN2 = Electrolytic Capacitor [capacitance=1µF package="100 mil [THT, electrolytic]"]
  C-IN1 = Ceramic Capacitor [capacitance=100nF package="100 mil [THT, multilayer]"]
  R24 = Resistor [tolerance=±5% resistance=10k package=THT]
  R25 = Resistor [tolerance=±5% resistance=10k package=THT]
  R27 = Resistor [tolerance=±5% resistance=10k package=THT]
  R28 = Resistor [tolerance=±5% resistance=10k package=THT]
  C-shft = Ceramic Capacitor [capacitance=100nF package="100 mil [THT, multilayer]"]
  LDR = Photocell (LDR) [package=THT]
  rLDR = Resistor [tolerance=±5% resistance=7k package=THT]
  R32 = Resistor [tolerance=±5% resistance=10k package=THT]
  R33 = Resistor [tolerance=±5% resistance=10k package=THT]
  R34 = Resistor [tolerance=±5% resistance=10k package=THT]
  C-N = Ceramic Capacitor [capacitance=100nF package="100 mil [THT, multilayer]"]
  shftOUT = female pin header, 9 pins [form="♀ (female)"]
  RTC-DS3231 = female pin header, 6 pins [form="♀ (female)"]
  BMP/BME = female pin header, 4 pins [form="♀ (female)"]
  5V_IN = rounded female pin header, 2 pins [form="♀ (female rounded)"]
  IRF4905_(3_3v) = Basic FET P-Channel [package="TO220 [THT]"]
  2N2222_(3_3v) = NPN-Transistor [package="TO92 [THT]"]
  R40 = Resistor [tolerance=±5% resistance=5k package=THT]
  R41 = Resistor [tolerance=±5% resistance=10k package=THT]
  ESP32 = ESP32S-HiLetgo [part_number="NodeMCU ESP32"]
  IRF4905_(sens) = Basic FET P-Channel [package="TO220 [THT]"]
  2N2222_(sens) = NPN-Transistor [package="TO92 [THT]"]
  R42 = Resistor [tolerance=±5% resistance=10k package=THT]
  R43 = Resistor [tolerance=±5% resistance=5k package=THT]
  ZS-042_RTC1 = ZS-042 RTC Module
  BME280 = BME280 Breakout
  C-RTC = Ceramic Capacitor [capacitance=100nF package="100 mil [THT, multilayer]"]
  C-BME = Ceramic Capacitor [capacitance=100nF package="100 mil [THT, multilayer]"]
  R45 = Resistor [tolerance=±5% resistance=220 package=THT]
  R46 = Resistor [tolerance=±5% resistance=220 package=THT]
  J1 = double row rounded female pin header, 6 pins [form="♀ (female rounded)"]
  J2 = double row rounded female pin header, 6 pins [form="♀ (female rounded)"]
  IRF4905_(sens2) = Basic FET P-Channel [package="TO220 [THT]"]
  2N2222_(sens2) = NPN-Transistor [package="TO92 [THT]"]
  R47 = Resistor [tolerance=±5% resistance=5k package=THT]
  R48 = Resistor [tolerance=±5% resistance=10k package=THT]
  logic = female pin header, 2 pins [form="♀ (female)"]
  sens2_(ext5v) = female pin header, 2 pins [form="♀ (female)"]
  RL1 = Resistor [tolerance=±5% resistance=4.7k package=THT]
  RL2 = Resistor [tolerance=±5% resistance=4.7k package=THT]
  74HC595 = 74HC595 [package="DIP16 [THT]"]
  ESP32_2 = rounded female pin header, 19 pins [form="♀ (female rounded)"]
  TX_RX = rounded female pin header, 2 pins [form="♀ (female rounded)"]
  qs_sh_st_ds = female pin header, 4 pins [form="♀ (female)"]
  lvl_shft = I2C level shifter bidirectional
  1N4731 = DIODE-ZENER [package=diode-zener]
  R49 = Resistor [tolerance=±5% resistance=10k package=THT]
  5V_Sw = Toggle Switch [package=THT]
  IRF4905_5V1 = Basic FET P-Channel [package="TO220 [THT]"]
  R50 = Resistor [tolerance=±5% resistance=220 package=THT]
  5V_IN_2 = LED - 3mm [color="Red (633nm)" package="3 mm [THT]"]
  SENS0 = rounded female pin header, 3 pins [form="♀ (female rounded)"]
  SENS1 = rounded female pin header, 3 pins [form="♀ (female rounded)"]
  SENS3 = rounded female pin header, 3 pins [form="♀ (female rounded)"]
  R59 = Resistor [tolerance=±5% resistance=220 package=THT]
  R60 = Resistor [tolerance=±5% resistance=220 package=THT]
  SENS2 = rounded female pin header, 3 pins [form="♀ (female rounded)"]
  R61 = Resistor [tolerance=±5% resistance=220 package=THT]
  R62 = Resistor [tolerance=±5% resistance=220 package=THT]
  sensor_(ext) = female alternating pin header, 1 pin [form="♀ (female)"]
  R63 = Resistor [tolerance=±5% resistance=220 package=THT]
  R64 = Resistor [tolerance=±5% resistance=220 package=THT]
  R65 = Resistor [tolerance=±5% resistance=220 package=THT]
  R66 = Resistor [tolerance=±5% resistance=220 package=THT]
  R67 = Resistor [tolerance=±5% resistance=220 package=THT]
  R68 = Resistor [tolerance=±5% resistance=220 package=THT]
  R69 = Resistor [tolerance=±5% resistance=220 package=THT]
  R70 = Resistor [tolerance=±5% resistance=220 package=THT]
  I2C = female pin header, 2 pins [form="♀ (female)"]
  1-Wire = female pin header, 3 pins [form="♀ (female)"]
  LDR_2 = Photocell (LDR) [package=THT]
  rLDR_2 = Resistor [tolerance=±5% resistance=7k package=THT]

nets:
  GND: C-IN2.-, C-IN1.0, R25.Pin_1, C-shft.0, rLDR.Pin_0, R32.Pin_0, R33.Pin_0, R34.Pin_0, C-N.0, RTC-DS3231.pin6, BMP/BME.pin2, 5V_IN.pin2, 2N2222_(3_3v).E, ESP32.GND, 2N2222_(sens).E, ZS-042_RTC1.GND, BME280.GND, C-RTC.1, C-BME.1, R46.Pin_0, J1.pin4, J1.pin5, J1.pin6, J2.pin4, J2.pin5, J2.pin6, 2N2222_(sens2).E, logic.pin2, sens2_(ext5v).pin2, 74HC595.GND, ESP32_2.pin14, lvl_shft.GND, R49.Pin_0, 5V_Sw.L1, R50.Pin_1, SENS0.pin3, SENS1.pin3, SENS3.pin3, R60.Pin_0, SENS2.pin3, R62.Pin_0, 1-Wire.pin3, rLDR_2.Pin_0
  VIN: C-IN2.+, C-IN1.1, R24.Pin_1, C-shft.1, C-N.1, R41.Pin_0, ESP32.VIN, IRF4905_(sens).source, R42.Pin_0, J1.pin1, J1.pin2, J1.pin3, IRF4905_(sens2).source, R48.Pin_0, 74HC595.VCC, ESP32_2.pin19, lvl_shft.HV, 1N4731.C, IRF4905_5V1.source, 5V_IN_2.anode, R63.Pin_1, R64.Pin_1, R65.Pin_1, R66.Pin_1, R67.Pin_1, R68.Pin_1, R69.Pin_1, R70.Pin_1
  N1: R24.Pin_0, 74HC595.MR
  N2: R25.Pin_0, shftOUT.pin9, 74HC595.OE, lvl_shft.HV4
  N3: R27.Pin_0, RTC-DS3231.pin3, BMP/BME.pin3, ESP32.GPIO22, ZS-042_RTC1.SCL, BME280.SCK/SCL, I2C.pin2
  VCC: R27.Pin_1, R28.Pin_1, LDR.pin_1, RTC-DS3231.pin5, BMP/BME.pin1, IRF4905_(3_3v).drain, IRF4905_(3_3v).source, ESP32.3.3, ZS-042_RTC1.VCC, BME280.3.3V, C-RTC.0, C-BME.0, J2.pin1, J2.pin2, J2.pin3, logic.pin1, ESP32_2.pin1, lvl_shft.LV, SENS0.pin1, SENS1.pin1, 1-Wire.pin1, LDR_2.pin_0
  N4: R28.Pin_0, RTC-DS3231.pin4, BMP/BME.pin4, ESP32.GPIO21, ZS-042_RTC1.SDA, BME280.SDI/SDA, I2C.pin1
  N5: LDR.pin_0, rLDR.Pin_1, ESP32.GPIO15
  N6: R32.Pin_1, 74HC595.ST_CP, qs_sh_st_ds.pin3, lvl_shft.HV2
  N7: R33.Pin_1, 74HC595.DS, qs_sh_st_ds.pin4, lvl_shft.HV3
  N8: R34.Pin_1, 74HC595.SH_CP, qs_sh_st_ds.pin2, lvl_shft.HV1
  N9: shftOUT.pin1, 74HC595.Q7, R63.Pin_0
  N10: shftOUT.pin2, 74HC595.Q6, R64.Pin_0
  N11: shftOUT.pin3, 74HC595.Q5, R65.Pin_0
  N12: shftOUT.pin4, 74HC595.Q4, R67.Pin_0
  N13: shftOUT.pin5, 74HC595.Q3, R68.Pin_0
  N14: shftOUT.pin6, 74HC595.Q2, R69.Pin_0
  N15: shftOUT.pin7, 74HC595.Q1, R70.Pin_0
  N16: shftOUT.pin8, 74HC595.Q0, R66.Pin_0
  N17: RTC-DS3231.pin1, ZS-042_RTC1.32K
  N18: RTC-DS3231.pin2, ZS-042_RTC1.SQW
  N19: 5V_IN.pin1, 5V_Sw.L2
  N20: IRF4905_(3_3v).gate, 2N2222_(3_3v).C, R41.Pin_1
  N21: 2N2222_(3_3v).B, R40.Pin_0
  N22: R40.Pin_1, ESP32.GPIO23
  N23: ESP32.EN, ESP32_2.pin2
  N24: ESP32.GPIO36, ESP32_2.pin3, SENS1.pin2
  N25: ESP32.GPIO39, R45.Pin_0, R46.Pin_1, ESP32_2.pin4
  N26: ESP32.GPIO34, ESP32_2.pin5, SENS0.pin2
  N27: ESP32.GPIO35, ESP32_2.pin6
  N28: ESP32.GPIO32, ESP32_2.pin7, lvl_shft.LV4
  N29: ESP32.GPIO33, ESP32_2.pin8
  N30: ESP32.GPIO25, R47.Pin_1, ESP32_2.pin9
  N31: ESP32.GPIO26, ESP32_2.pin10, R59.Pin_1, R60.Pin_1
  N32: ESP32.GPIO27, ESP32_2.pin11, R61.Pin_1, R62.Pin_1
  N33: ESP32.GPIO14, ESP32_2.pin12
  N34: ESP32.GPIO12, ESP32_2.pin13
  N35: ESP32.GPIO13, ESP32_2.pin15, lvl_shft.LV3
  N36: ESP32.GPIO9, ESP32_2.pin16
  N37: ESP32.GPIO10, ESP32_2.pin17
  N38: ESP32.GPIO11, ESP32_2.pin18
  N39: ESP32.GPIO4, R43.Pin_1
  N40: ESP32.GPIO16, lvl_shft.LV1
  N41: ESP32.GPIO17, lvl_shft.LV2
  N42: ESP32.GPIO5, 1-Wire.pin2
  N43: ESP32.GPIO18, LDR_2.pin_1, rLDR_2.Pin_1
  N44: ESP32.GPIO3, TX_RX.pin1
  N45: ESP32.GPIO1, TX_RX.pin2
  N46: IRF4905_(sens).gate, 2N2222_(sens).C, R42.Pin_1, RL1.Pin_1
  N47: IRF4905_(sens).drain, RL1.Pin_0, SENS3.pin1, SENS2.pin1
  N48: 2N2222_(sens).B, R43.Pin_0
  N49: R45.Pin_1, sensor_(ext).pin1
  N50: IRF4905_(sens2).gate, 2N2222_(sens2).C, R48.Pin_1, RL2.Pin_1
  N51: IRF4905_(sens2).drain, sens2_(ext5v).pin1, RL2.Pin_0
  N52: 2N2222_(sens2).B, R47.Pin_0
  N53: 74HC595.Q7', qs_sh_st_ds.pin1
  N54: 1N4731.A, R49.Pin_1, IRF4905_5V1.gate
  N55: 5V_Sw.COM, IRF4905_5V1.drain
  N56: R50.Pin_0, 5V_IN_2.cathode
  N57: SENS3.pin2, R59.Pin_0
  N58: SENS2.pin2, R61.Pin_0

notes:
  SCL
  SDA
  VCC
  GND
  32K
  SQW
  5V
  3.3V
  PWM
  + -
  15mm socket
  0
  7
  6
  5
  4
  3
  2
  1
  - +
  3V Sensors (max 200 mA)
  5V Sensors
  DAT
  br-mat (c) 2023
  Board  5v5
  bewae v3.3
  github.com/br-mat

custom parts:
  ESP32S-HiLetgo: HiLetgo ESP-WROOM-32 ESP32 ESP-32S Development Board 2.4GHz Dual-Mode WiFi + Bluetooth Dual Cores Microcontroller The ESP32 integrated with Antenna switches, RF Balun, power amplifiers, low-noise amplifiers, filters, and management modules, and the entire solution occupies the least area of PCB. 2.4 GHz Wi-Fi plus Bluetooth dual-mode chip, with TSMC Ultra-low power consumption 40nm technology,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
